# Fritzing sketch esp32 lcd co2 (saved by Fritzing 0.9.3b)
breadboards: 1

parts:
  MH-Z2 = MH-Z14 [part_number=MH-Z14]
  Part8 = Logic Level Converter
  U1 = lolin
  R1 = TRIMPOT [package=trim_pot_pth]
  LCD_I2C1 = LCD I2C [package="DIP (Dual Inline) [THT]"]

nets (from the schematic view):
  N1: MH-Z2.1, MH-Z2.15, Part8.HV, U1.connector14, LCD_I2C1.VCC
  GND: MH-Z2.2, MH-Z2.3, Part8.GND, U1.connector20, LCD_I2C1.GND
  N2: MH-Z2.4, U1.connector2
  N3: MH-Z2.6, U1.connector12
  N4: MH-Z2.10, MH-Z2.13, U1.connector24
  N5: MH-Z2.11, MH-Z2.14, U1.connector23
  N6: Part8.TX2_LV, U1.connector32
  N7: Part8.RX2_LV, U1.connector33
  N8: Part8.LV, U1.connector34
  N9: Part8.RX2_HV, LCD_I2C1.SCL
  N10: Part8.TX2_HV, LCD_I2C1.SDA
  N11: R1.WIPER, LCD_I2C1.LED_1
  N12: R1.CW, LCD_I2C1.LED_2

custom parts:
  MH-Z14: MH-Z14 NDIR Infrared gas module is a common type, small size sensor, using non-dispersive infrared (NDIR) principle to detect the existence of CO2 in the air, with good selectivity, non-oxygen dependant, long life. Built-in temperature sensor can do temperature compensation; and it has digital output and analog voltage output.
